# Fritzing sketch HS_project (saved by Fritzing 0.9.3b)
breadboards: 1

parts:
  S1 = Pushbutton [package="[THT]"]
  S2 = Pushbutton [package="[THT]"]
  S3 = Pushbutton [package="[THT]"]
  S4 = Pushbutton [package="[THT]"]
  S5 = Pushbutton [package="[THT]"]
  S6 = Pushbutton [package="[THT]"]
  S7 = Pushbutton [package="[THT]"]
  Part1 = Arduino Leonardo (Rev3b)
  Part2 = Arduino Nano (Rev3.0)
  U1 = POT [package=pot_alpha_rv16af-20]
  7_Segment4 = 7 Segment Display
  R1 = Resistor [tolerance=±5% resistance=220 package=THT]

nets:
  N1: S1.Pin_1, S1.Pin_2, S2.Pin_1, S2.Pin_2, S3.Pin_1, S3.Pin_2, S4.Pin_1, S4.Pin_2, S5.Pin_1, S5.Pin_2, S6.Pin_1, S6.Pin_2, S7.Pin_1, S7.Pin_2, Part1.GND, U1.A
  N2: S1.Pin_3, S1.Pin_4, Part1.D13_PWM
  N3: S2.Pin_3, S2.Pin_4, Part1.D12/A11
  N4: S3.Pin_3, S3.Pin_4, Part1.D11_PWM
  N5: S4.Pin_3, S4.Pin_4, Part1.D10_PWM/A10
  N6: S5.Pin_3, S5.Pin_4, Part1.D9_PWM/A9
  N7: S6.Pin_3, S6.Pin_4, Part1.D8/A8
  N8: S7.Pin_3, S7.Pin_4, Part1.D2/SDA
  N9: Part1.D4/A6, Part2.D10
  N10: Part1.D5_PWM, Part2.D11/MOSI
  N11: Part1.D6_PWM/A7, Part2.D12/MISO
  N12: Part1.5V, U1.E
  N13: Part1.A3, U1.S
  N14: Part2.D2, 7_Segment4.Segment_A
  N15: Part2.D3, 7_Segment4.Segment_F
  N16: Part2.D4, 7_Segment4.Segment_B
  N17: Part2.D5, 7_Segment4.Segment_E
  N18: Part2.D6, 7_Segment4.Segment_D
  N19: Part2.D7, 7_Segment4.Segment_C
  N20: Part2.D8, 7_Segment4.Segment_G
  N21: Part2.D13/SCK, R1.Pin_1
  N22: 7_Segment4.common_anode, R1.Pin_0
