# Fritzing sketch simon_says (saved by Fritzing 0.9.3b)
breadboards: 1

parts:
  Componente1 = Arduino Nano (Rev3.0)
  S1 = Momentary Switch [package=ksa_sealed_tac_switch]
  S2 = Momentary Switch [package=ksa_sealed_tac_switch]
  S3 = Momentary Switch [package=ksa_sealed_tac_switch]
  S4 = Momentary Switch [package=ksa_sealed_tac_switch]
  LED1 = smd LED [color="Red (633nm)" package="0805 [SMD]"]
  LED2 = smd LED [color="Red (633nm)" package="0805 [SMD]"]
  LED3 = smd LED [color="Red (633nm)" package="0805 [SMD]"]
  LED4 = smd LED [color="Red (633nm)" package="0805 [SMD]"]
  R1 = Resistor [tolerance=±5% resistance=220 package=THT]
  R2 = Resistor [tolerance=±5% resistance=220 package=THT]
  R3 = Resistor [tolerance=±5% resistance=220 package=THT]
  R4 = Resistor [tolerance=±5% resistance=220 package=THT]

nets:
  N1: Componente1.GND, S1.2, S2.2, S3.2, S4.2, LED1.cathode, LED2.cathode, LED3.cathode, LED4.cathode
  N2: Componente1.D5, R3.Pin_1
  N3: Componente1.D6, R2.Pin_1
  N4: Componente1.D7, R1.Pin_1
  N5: Componente1.D8, R4.Pin_1
  N6: Componente1.D9, S4.3
  N7: Componente1.D10, S3.3
  N8: Componente1.D11/MOSI, S2.3
  N9: Componente1.D12/MISO, S1.3
  N10: LED1.anode, R4.Pin_0
  N11: LED2.anode, R1.Pin_0
  N12: LED3.anode, R2.Pin_0
  N13: LED4.anode, R3.Pin_0
