# Fritzing sketch schematic (saved by Fritzing 0.9.10b)
breadboards: 1

parts:
  Part1 = Arduino Nano (Rev3.0)
  HC-SR04_Sensor_1 = HC-SR04 Ultrasonic Distance Sensor
  HC-SR04_Sensor_2 = HC-SR04 Ultrasonic Distance Sensor
  U1 = 7-SEGMENT-4DIGIT [package=7-segment-4digit]  # not connected

nets:
  GND: Part1.GND, HC-SR04_Sensor_1.GND, HC-SR04_Sensor_2.GND
  N1: Part1.D2, HC-SR04_Sensor_1.ECHO
  N2: Part1.D3, HC-SR04_Sensor_1.TRIG
  N3: Part1.D4, HC-SR04_Sensor_2.ECHO
  N4: Part1.D5, HC-SR04_Sensor_2.TRIG
  VCC: Part1.5V, HC-SR04_Sensor_1.VCC, HC-SR04_Sensor_2.VCC

notes:
  7 segment format:
  d1 A F d2 d3 B
  E D P C G d4
  distance between sensors receivers = 9 cm
